# Fritzing sketch ESP8266PhotocouplerLED (saved by Fritzing 0.9.2b)
breadboards: 1

parts:
  U1 = ESP8266 NodeMCU LoLin base
  V1 = DC Power [voltage=3.3V]
  V2 = DC Power [voltage=12V]
  Q1 = PHOTOTRANSISTOR REFLECTIVE OBJECT SENSOR [package=qrb1114-side]
  Q2 = Basic FET P-Channel [package="TO220 [THT]"]
  R2 = Resistor [tolerance=±5% resistance=1k package=THT]
  R3 = Resistor [tolerance=±5% resistance=10k package=THT]
  LED = LEDs [package=led10mm]
  R1 = Resistor [tolerance=±5% resistance=390 package=THT]

nets:
  N1: U1.connector3, V1.V-, R1.Pin_1
  N2: U1.connector12, Q1.A
  N3: U1.connector29, V1.V+
  N4: V2.V+, R3.Pin_1, LED.A
  N5: V2.V-, Q2.source, R2.Pin_1
  N6: Q1.C, Q2.gate, R3.Pin_0
  N7: Q1.E, R2.Pin_0
  N8: Q1.K, R1.Pin_0
  N9: Q2.drain, LED.C
